# Fritzing sketch LampSchematic (saved by Fritzing 0.9.10b)
breadboards: 1

parts:
  M5Stack-ATOM-Matrix1 = atom-matrix [package=M5Stack]
  Button = Pushbutton [package="[THT]"]
  NEOPIXEL1 = Neopixel Strip -- White (30/m)
  Knob = Angle Sensor
  Proximity_Sensor = TOF

nets:
  N1: M5Stack-ATOM-Matrix1.G21, Button.Pin_3, Button.Pin_4
  N2: M5Stack-ATOM-Matrix1.G25, NEOPIXEL1.Din
  N3: M5Stack-ATOM-Matrix1.G32, Proximity_Sensor.SCL
  N4: M5Stack-ATOM-Matrix1.G26, Proximity_Sensor.SDA
  VCC: M5Stack-ATOM-Matrix1.5Vb, NEOPIXEL1.+5V, Knob.VCC, Proximity_Sensor.VCC
  GND: M5Stack-ATOM-Matrix1.GNDb, Button.Pin_1, NEOPIXEL1.GND, Knob.GND, Proximity_Sensor.GND
  N5: M5Stack-ATOM-Matrix1.G33, Knob.IN
  N6: M5Stack-ATOM-Matrix1.G23, Knob.OUT

custom parts:
  atom-matrix: M5Stack ATOM Matrix
  Neopixel Strip -- White (30/m): These NeoPixel strips have 30 digitally-addressable pixel LEDs per meter and are very affordable and are only 12.5 mm wide, 10 mm if you remove the strip from the casing.
  Angle Sensor: The Angle sensor is a simple potentiometer which changes the resistance in the circuit when twisted
  TOF: TOF(Time of Flight) is a high accuracy distance sensor which has a range of up to 2 metres. It uses the VL53L0X chip
